# Fritzing sketch GGVib (saved by Fritzing 0.9.3b)
breadboards: 1

parts:
  Transistor = MOSFET-NCHANNEL [package=to-92]
  Vibration_motor = Vibration Motor- ROB-08449 [package=vibe-motor-10mm]
  Pull-down_resistor = Resistor [tolerance=±5% resistance=1k package="2512 [SMD]"]
  part = screw terminal, 5 pins [part_number=micro:bit]

nets:
  N1: Transistor.D, Vibration_motor.-
  N2: Transistor.S, part.pin5
  N3: Transistor.G, Pull-down_resistor.Pin_1
  N4: Vibration_motor.+, part.pin4
  N5: Pull-down_resistor.Pin_0, part.pin3

notes:
  0
  2
  1
  3V
  GND
